// Logisim project zd1_Illia_Ponomarov.circ as structural Verilog: 1 circuit, main circuit main
// AB~CD+ABC~D+~ACD+~A~D~C+~BCD+~B~D~C
module main (
  input  A,
  input  B,
  input  C,
  input  D,
  output Y_zad,
  output Z_zad,
  output Y_DNF,
  output Z_DNF,
  output Y_KNF,
  output Z_KNF
);

  wire _1_NAND_out, _2_XNOR_out, _3_XOR_out, AB_nCD_out, ABC_nD_out, B_nC_out, B_nD_out, BCD_out, C_nB_out,
       C_nD_A_out, C_nD_B_out, D_nB_out, D_nC_A_out, D_nC_B_out, nA_nB_D_C_out, nA_nB_nC_nD_out,
       nA_nD_nC_out, nACD_out, nB_nD_nC_out, nBCD_out, not_1_out, not_2_out, not_3_out, not_4_out, not_5_out,
       not_6_out, not_7_out, not_8_out, not_9_out;

  not not_1 (not_1_out, D);
  not not_2 (not_2_out, C);
  not not_3 (not_3_out, D);
  not not_4 (not_4_out, A);
  not not_5 (not_5_out, B);
  not not_6 (not_6_out, A);
  not not_7 (not_7_out, B);
  not not_8 (not_8_out, C);
  not not_9 (not_9_out, D);
  nand _1_NAND (_1_NAND_out, A, B);
  xnor _2_XNOR (_2_XNOR_out, C, not_1_out);
  xor _3_XOR (_3_XOR_out, B, D);
  and AB_nCD (AB_nCD_out, A, B, not_2_out, D);
  and ABC_nD (ABC_nD_out, A, B, C, not_3_out);
  and nACD (nACD_out, not_4_out, C, D);
  and nA_nD_nC (nA_nD_nC_out, not_4_out, not_2_out, not_3_out);
  and nBCD (nBCD_out, not_5_out, C, D);
  and nB_nD_nC (nB_nD_nC_out, not_5_out, not_3_out, not_2_out);
  and BCD (BCD_out, B, C, D);
  or nA_nB_nC_nD (nA_nB_nC_nD_out, not_6_out, not_7_out, not_8_out, not_9_out);
  or nA_nB_D_C (nA_nB_D_C_out, not_6_out, not_7_out, C, D);
  or C_nD_B (C_nD_B_out, C, not_9_out, B);
  or C_nD_A (C_nD_A_out, C, not_9_out, A);
  or D_nC_A (D_nC_A_out, D, not_8_out, A);
  or D_nC_B (D_nC_B_out, D, not_8_out, B);
  or C_nB (C_nB_out, not_7_out, C);
  or D_nB (D_nB_out, D, not_7_out);
  or B_nC (B_nC_out, B, not_8_out);
  or B_nD (B_nD_out, B, not_9_out);
  xor _4_XOR (Y_zad, _1_NAND_out, _2_XNOR_out);
  nor _5_NOR (Z_zad, _2_XNOR_out, _3_XOR_out);
  and and_1 (Y_KNF, nA_nB_nC_nD_out, nA_nB_D_C_out, C_nD_B_out, C_nD_A_out, D_nC_A_out, D_nC_B_out);
  and and_2 (Z_KNF, C_nB_out, D_nB_out, B_nC_out, B_nD_out);
  or or_1 (Y_DNF, AB_nCD_out, ABC_nD_out, nACD_out, nA_nD_nC_out, nBCD_out, nB_nD_nC_out);
  or or_2 (Z_DNF, BCD_out, nB_nD_nC_out);

  // Notes on the sheet:
  //   DNF FORM
  //   KNF FORM
  //   AB~CD+ABC~D+~ACD+~A~D~C+~BCD+~B~D~C
  //   BCD+!B!C!D
  //   (~A+~B+~C+~D)*(~A+~B+D+C)*(C+~D+B)*(C+~D+A)*(D+~C+A)*(D+~C+B)
  //   (C+~B)(D+~B)(B+~C)(B+~D)
endmodule
