// Logisim project zadanie2_Illia_Ponomarov.circ as structural Verilog: 1 circuit, main circuit main
module main (
  input  a,
  input  b,
  input  c,
  input  d,
  output A_D,
  output B_D,
  output C_D,
  output D_D,
  output A_K,
  output B_K,
  output C_K,
  output D_K
);

  wire n_a___nc__d_out, n_a__b_out, n_a_nd_out, n_b___c___d___a_out, n_b___d___a_out, n_b___nd___nc_out,
       n_b___nd_out, n_b_nc_nd_out, n_b_nc_out, n_bd_out, n_c___d_out, n_c___nb___nd_out, n_c_nd_out,
       n_d___nb___nc___a_out, n_na___nb___nd_out, n_na___nd___nc_out, n_nabcd_out, n_nb___nd_out,
       n_nb_ncd_out, n_nbc_nd_out, n_nbd_out, n_nc___d___a_out, n_nc___nb___a_out, n_nc___nb___nd_out,
       na_2_out, na_out, nb_2_out, nb_out, nc_2_out, nc_out, nd_2_out, nd_out;

  nand nb (nb_out, b, b);
  nand na (na_out, a, a);
  nor na_2 (na_2_out, a, a);
  nor nb_2 (nb_2_out, b, b);
  nand nc (nc_out, c, c);
  nand nd (nd_out, d, d);
  nor nc_2 (nc_2_out, c, c);
  nor nd_2 (nd_2_out, d, d);
  nand n_b_nc_nd (n_b_nc_nd_out, b, nc_out, nd_out);
  nand n_bd (n_bd_out, b, d);
  nand n_a_nd (n_a_nd_out, a, nd_out);
  nand n_c_nd (n_c_nd_out, c, nd_out);
  nand n_b_nc (n_b_nc_out, b, nc_out);
  nand n_nbd (n_nbd_out, nb_out, d);
  nand n_nabcd (n_nabcd_out, na_out, b, c, d);
  nand n_nbc_nd (n_nbc_nd_out, nb_out, c, nd_out);
  nand n_nb_ncd (n_nb_ncd_out, nb_out, nc_out, d);
  nor n_a__b (n_a__b_out, a, b);
  nor n_b___nd (n_b___nd_out, b, nd_2_out);
  nor n_a___nc__d (n_a___nc__d_out, a, nc_2_out, d);
  nor n_c___d (n_c___d_out, c, d);
  nor n_nb___nd (n_nb___nd_out, nb_2_out, nd_2_out);
  nor n_b___d___a (n_b___d___a_out, b, a, d);
  nor n_nc___nb___a (n_nc___nb___a_out, a, nc_2_out, nb_2_out);
  nor n_nc___nb___nd (n_nc___nb___nd_out, nc_2_out, nb_2_out, nd_2_out);
  nor n_nc___d___a (n_nc___d___a_out, nc_2_out, d, a);
  nor n_b___nd___nc (n_b___nd___nc_out, b, nc_2_out, nd_2_out);
  nor n_na___nb___nd (n_na___nb___nd_out, na_2_out, nb_2_out, nd_2_out);
  nor n_na___nd___nc (n_na___nd___nc_out, na_2_out, nd_2_out, nc_2_out);
  nor n_b___c___d___a (n_b___c___d___a_out, a, b, c, d);
  nor n_c___nb___nd (n_c___nb___nd_out, c, nb_2_out, nd_2_out);
  nor n_d___nb___nc___a (n_d___nb___nc___a_out, d, nb_2_out, a, nc_2_out);
  nand nand_1 (A_D, n_b_nc_nd_out, n_bd_out, n_a_nd_out);
  nand nand_2 (B_D, n_c_nd_out, n_nbd_out);
  nand nand_3 (C_D, n_b_nc_out, n_nbd_out, n_a_nd_out);
  nand nand_4 (D_D, n_nabcd_out, n_nbc_nd_out, n_nb_ncd_out, n_b_nc_nd_out, n_a_nd_out);
  nor nor_1 (A_K, n_a__b_out, n_b___nd_out, n_a___nc__d_out);
  nor nor_2 (B_K, n_c___d_out, n_nb___nd_out);
  nor nor_3 (C_K, n_b___d___a_out, n_nc___nb___a_out, n_nc___nb___nd_out, n_nc___d___a_out);
  nor nor_4 (D_K, n_b___nd___nc_out, n_na___nb___nd_out, n_na___nd___nc_out, n_b___c___d___a_out, n_c___nb___nd_out, n_d___nb___nc___a_out);

  // Notes on the sheet:
  //   A = !(!(b !c !d) !(b d) !(a !d))
  //   B = !(!(c !d) !(!b d))
  //   C = !(!(b !c) !(!b d) !(a !d))
  //   D = !( !(!a b c d) !(!b c !d) !(!b !c d) (b !c !d) !(a !d))
  //   A = !( !(a + b) + !(b + !d) + !(a + !c +d ))
  //   B = !( !(c + d) + !(!b + !d)))
  //   C = !( (b + d + a) + !(!c + !b + a) + !(!c + !b + !d) + !(!c + d + a))
  //   D = !(!(!a + !b + !d) + !(!a + !d + !c ) + !(b + c + d + a) + (b + !d + !c) + !(c + !b + !d) + !(d + !b + !c + a)
endmodule
