// Logisim project zd3_Illia_Ponomarov (1).circ as structural Verilog: 1 circuit, main circuit main
module main (
  input  X,
  input  Res,
  output Y
);

  wire CLK_out, J1_out, J2_out, j_k_ff_1_q, j_k_ff_1_qn, j_k_ff_2_q, j_k_ff_2_qn, j_k_ff_3_q, j_k_ff_3_qn,
       K1_out, K2_out, K3_out, nand_1_out, nand_2_out, nand_3_out, nand_4_out, nand_5_out, nand_6_out,
       nand_7_out, nand_8_out, nand_9_out, nand_10_out, nand_11_out;

  nand nand_1 (nand_1_out, X, X);
  Clock CLK (.out(CLK_out));
  nand nand_2 (nand_2_out, j_k_ff_1_q, j_k_ff_2_q);
  nand nand_3 (nand_3_out, nand_1_out, j_k_ff_2_q, j_k_ff_3_q);
  nand K1 (K1_out, j_k_ff_2_qn, nand_1_out);
  nand nand_4 (nand_4_out, X, j_k_ff_1_q);
  nand nand_5 (nand_5_out, nand_1_out, j_k_ff_3_q);
  nand nand_6 (nand_6_out, nand_1_out, j_k_ff_3_q);
  nand nand_7 (nand_7_out, X, j_k_ff_3_q);
  nand nand_8 (nand_8_out, j_k_ff_1_q, j_k_ff_2_qn, j_k_ff_3_qn);
  nand nand_9 (nand_9_out, nand_1_out, j_k_ff_2_q);
  nand nand_10 (nand_10_out, nand_1_out, j_k_ff_2_qn, j_k_ff_3_q);
  nand J1 (J1_out, nand_3_out, nand_3_out);
  nand J2 (J2_out, nand_4_out, nand_5_out);
  nand K2 (K2_out, nand_6_out, j_k_ff_2_q, nand_7_out);
  nand nand_11 (nand_11_out, nand_8_out, nand_1_out);
  nand K3 (K3_out, nand_9_out, nand_10_out);
  nand nand_12 (Y, nand_2_out, nand_2_out);
  J_K_Flip_Flop j_k_ff_1 (
    .J(J1_out), .clk(CLK_out), .K(K1_out), .Q(j_k_ff_1_q), .Qn(j_k_ff_1_qn), .reset(Res));  // open: preset, en
  J_K_Flip_Flop j_k_ff_2 (
    .J(J2_out), .clk(CLK_out), .K(K2_out), .Q(j_k_ff_2_q), .Qn(j_k_ff_2_qn), .reset(Res));  // open: preset, en
  J_K_Flip_Flop j_k_ff_3 (
    .J(nand_11_out), .clk(CLK_out), .K(K3_out), .Q(j_k_ff_3_q), .Qn(j_k_ff_3_qn), .reset(Res));  // open: preset, en

  // Notes on the sheet:
  //   Z1
  //   Z2
  //   !Z1
  //   !Z3
  //   Z3
  //   !Z2
  //   J3
endmodule
